# Fritzing sketch PoolClockWiringDiagram (saved by Fritzing 0.9.3b)
circuit board: 8.46667cm x 5.64444cm

parts:
  WS2812B_60_Leds/m_IP30 = WS2812 RGB LED strip
  WS2812B_60_Leds/m_IP30_2 = WS2812 RGB LED strip
  Photosensitive_Sensor = LM393 phototransistor breakout
  5_5_x_2_1mm = 2.1mm DC Barrel Jack [part_number="Power Connector"]
  Power_ON/OFF = Round Pushbutton
  Air_Temp_sensor = AM2320 Humidity and Temperature Sensor [part_number=AM2320]
  Water_Temp_sensor = DS18B20 1-Wire Temperature Sensor Probe [part_number="DS18B20 Probe"]
  S2 = Pushbutton [part_number=+ package="[SMD]"]
  S3 = Pushbutton [part_number=">> / ||" package="[SMD]"]
  S4 = Pushbutton [part_number=- package="[SMD]"]
  R1 = Resistor [tolerance=±5% resistance=330 package="0402 [SMD]"]
  R2 = Resistor [tolerance=±5% resistance=10k package="0402 [SMD]"]
  R3 = Resistor [tolerance=±5% resistance=10k package="0402 [SMD]"]
  R4 = Resistor [tolerance=±5% resistance=10k package="0402 [SMD]"]
  R5 = Resistor [tolerance=±5% resistance=10k package="0402 [SMD]"]
  S1 = Pushbutton [part_number=Mode package="[THT]"]
  ESP32-VROOM-32U = ESP32-38PinWide [part_number=ESP32-38PinWide]
  LCD2004-I2C1 = LCD2004-I2C
  R6 = Resistor [tolerance=±5% resistance=10k package="0402 [SMD]"]
  R7 = Resistor [tolerance=±5% resistance=10k package="0402 [SMD]"]
  R8 = Resistor [tolerance=±5% resistance=4.7k package="0402 [SMD]"]
  C1 = Electrolytic Capacitor [capacitance=1000μF package="1010 [SMD, electrolytic]"]
  PIR_HC-SR501 = HC-SR501 Body Sensor Module

nets (from the breadboard view):
  GND: WS2812B_60_Leds/m_IP30.GND#0, Photosensitive_Sensor.GND, 5_5_x_2_1mm.sleeve, Air_Temp_sensor.GND, Water_Temp_sensor.GND, R2.Pin_0, R3.Pin_0, R4.Pin_0, R5.Pin_0, ESP32-VROOM-32U.GND, LCD2004-I2C1.GND, C1.-, PIR_HC-SR501.GND
  VCC: WS2812B_60_Leds/m_IP30.VCC#1, Photosensitive_Sensor.VCC, Power_ON/OFF.leg1, Air_Temp_sensor.VDD, Water_Temp_sensor.VDD, S2.Pin_3, S2.Pin_4, S3.Pin_3, S3.Pin_4, S4.Pin_3, S4.Pin_4, S1.Pin_3, ESP32-VROOM-32U.VIN, LCD2004-I2C1.VCC, R6.Pin_1, R7.Pin_1, R8.Pin_0, C1.+, PIR_HC-SR501.VCC
  N1: WS2812B_60_Leds/m_IP30.DIN, R1.Pin_1
  N2: WS2812B_60_Leds/m_IP30.GND#4, WS2812B_60_Leds/m_IP30_2.GND
  N3: WS2812B_60_Leds/m_IP30.VCC#5, WS2812B_60_Leds/m_IP30_2.VCC
  N4: WS2812B_60_Leds/m_IP30.DOUT, WS2812B_60_Leds/m_IP30_2.DIN
  N5: Photosensitive_Sensor.DO, ESP32-VROOM-32U.GPIO19
  N6: 5_5_x_2_1mm.center, Power_ON/OFF.leg0
  N7: Air_Temp_sensor.SDA, ESP32-VROOM-32U.GPIO21, LCD2004-I2C1.SDA, R7.Pin_0
  N8: Air_Temp_sensor.SCL, ESP32-VROOM-32U.GPIO22, LCD2004-I2C1.SCL, R6.Pin_0
  N9: Water_Temp_sensor.DQ, ESP32-VROOM-32U.GPIO4, R8.Pin_1
  N10: S2.Pin_1, S2.Pin_2, R3.Pin_1, ESP32-VROOM-32U.GPIO14
  N11: S3.Pin_1, S3.Pin_2, R4.Pin_1, ESP32-VROOM-32U.GPIO27
  N12: S4.Pin_1, S4.Pin_2, R5.Pin_1, ESP32-VROOM-32U.GPIO26
  N13: R1.Pin_0, ESP32-VROOM-32U.GPIO18
  N14: R2.Pin_1, S1.Pin_1, S1.Pin_2, ESP32-VROOM-32U.GPIO12
  N15: ESP32-VROOM-32U.GPIO25, PIR_HC-SR501.OUT

custom parts:
  WS2812 RGB LED strip: WS2812 strip
  2.1mm DC Barrel Jack: 2.1mm DC Barrel Jack with Thru-Hole Connectors (breadboardable)
  AM2320 Humidity and Temperature Sensor: AM2320 I2C Humidity and Temperature Sensor
  ESP32-38PinWide: Generic 38-Pin ESP32 with wide format (only access to one side of pins on a breadboard) based on Stephen Lilley's HiLetgo ESP-WROOM-32 ESP32 ESP-32S Development Board.
  LCD2004-I2C: A standard character display with 4x20 characters. Comes in many colors with LCM2004 IIC attached.
  HC-SR501 Body Sensor Module: Pyroelectric Infrared PIR Motion Sensor Detector Module
